# Fritzing sketch Stepper Driver Board (saved by Fritzing 0.9.3b)
circuit board: 10cm x 10cm
breadboards: 1

parts:
  DRV_3 = DRV 8825 Stepper Motor Carrier, High Current [part_number="DRV 8825"]
  Arduino_Mega = Arduino Mega 2560 (Rev3)
  DRV_4 = DRV 8825 Stepper Motor Carrier, High Current [part_number="DRV 8825"]
  DRV_1 = DRV 8825 Stepper Motor Carrier, High Current [part_number="DRV 8825"]
  DRV_2 = DRV 8825 Stepper Motor Carrier, High Current [part_number="DRV 8825"]
  DRV_5 = DRV 8825 Stepper Motor Carrier, High Current [part_number="DRV 8825"]
  DRV_6 = DRV 8825 Stepper Motor Carrier, High Current [part_number="DRV 8825"]
  1_2_3_4_5_6_7_8 = double row female pin header, 16 pins [form="♀ (female)"]
  +12- = female pin header, 2 pins [form="♀ (female)"]
  C = Electrolytic Capacitor [capacitance=1µF package="200 mil [THT, electrolytic]"]
  DRV_7 = DRV 8825 Stepper Motor Carrier, High Current [part_number="DRV 8825"]
  DRV_8 = DRV 8825 Stepper Motor Carrier, High Current [part_number="DRV 8825"]
  +12-_2 = female pin header, 2 pins [form="♀ (female)"]
  +12-_3 = female pin header, 2 pins [form="♀ (female)"]
  +5- = female pin header, 2 pins [form="♀ (female)"]
  1 = female pin header, 4 pins [form="♀ (female)"]
  2 = female pin header, 4 pins [form="♀ (female)"]
  3 = female pin header, 4 pins [form="♀ (female)"]
  4 = female pin header, 4 pins [form="♀ (female)"]
  +FAN- = female pin header, 2 pins [form="♀ (female)"]
  +FAN-_2 = female pin header, 2 pins [form="♀ (female)"]
  5 = female pin header, 4 pins [form="♀ (female)"]
  6 = female pin header, 4 pins [form="♀ (female)"]
  7 = female pin header, 4 pins [form="♀ (female)"]
  8 = female pin header, 4 pins [form="♀ (female)"]
  C1 = Electrolytic Capacitor [capacitance=1µF package="200 mil [THT, electrolytic]"]
  R1 = Resistor [tolerance=±5% resistance=10k package=THT]
  R2 = Resistor [tolerance=±5% resistance=10k package=THT]
  R3 = Resistor [tolerance=±5% resistance=10k package=THT]
  R4 = Resistor [tolerance=±5% resistance=10k package=THT]
  R6 = Resistor [tolerance=±5% resistance=10k package=THT]
  R7 = Resistor [tolerance=±5% resistance=10k package=THT]
  R8 = Resistor [tolerance=±5% resistance=10k package=THT]
  R9 = Resistor [tolerance=±5% resistance=10k package=THT]

nets:
  N1: DRV_3.ENABLE, Arduino_Mega.D7_PWM
  N2: DRV_3.RESET, DRV_3.SLEEP, Arduino_Mega.5V, DRV_4.RESET, DRV_4.SLEEP, DRV_1.RESET, DRV_1.SLEEP, DRV_2.RESET, DRV_2.SLEEP, DRV_5.RESET, DRV_5.SLEEP, DRV_6.RESET, DRV_6.SLEEP, 1_2_3_4_5_6_7_8.pin1, 1_2_3_4_5_6_7_8.pin2, 1_2_3_4_5_6_7_8.pin3, 1_2_3_4_5_6_7_8.pin4, 1_2_3_4_5_6_7_8.pin5, 1_2_3_4_5_6_7_8.pin6, 1_2_3_4_5_6_7_8.pin7, 1_2_3_4_5_6_7_8.pin8, DRV_7.RESET, DRV_7.SLEEP, DRV_8.RESET, DRV_8.SLEEP
  N3: DRV_3.STEP, Arduino_Mega.D8_PWM
  N4: DRV_3.DIRECTION, Arduino_Mega.D9_PWM
  N5: DRV_3.VOLTAGE_ST/_MT, DRV_4.VOLTAGE_ST/_MT, DRV_1.VOLTAGE_ST/_MT, DRV_2.VOLTAGE_ST/_MT, +12-.pin2, C.+
  N6: DRV_3.GROUND_ST/_MT, DRV_4.GROUND_ST/_MT, DRV_1.GROUND_ST/_MT, DRV_2.GROUND_ST/_MT, +12-.pin1, C.-
  N7: DRV_3.OUT_2B, 3.pin1
  N8: DRV_3.OUT_2A, 3.pin2
  N9: DRV_3.OUT_1A, 3.pin3
  N10: DRV_3.OUT_1B, 3.pin4
  N11: DRV_3.GROUND_LOG, Arduino_Mega.GND, DRV_4.GROUND_LOG, DRV_1.GROUND_LOG, DRV_2.GROUND_LOG, DRV_5.DIRECTION, DRV_5.GROUND_LOG, DRV_6.GROUND_LOG, DRV_7.ENABLE, DRV_7.GROUND_LOG, DRV_8.GROUND_LOG, +5-.pin1, R1.Pin_0, R2.Pin_0, R3.Pin_0, R4.Pin_0, R6.Pin_0, R7.Pin_0, R8.Pin_0, R9.Pin_0
  N12: Arduino_Mega.D18/TX1, DRV_1.ENABLE
  N13: Arduino_Mega.VIN, +5-.pin2
  N14: Arduino_Mega.D2_PWM, DRV_1.STEP
  N15: Arduino_Mega.D3_PWM, DRV_1.DIRECTION
  N16: Arduino_Mega.D23, 1_2_3_4_5_6_7_8.pin9, R1.Pin_1
  N17: Arduino_Mega.D25, 1_2_3_4_5_6_7_8.pin10, R2.Pin_1
  N18: Arduino_Mega.D27, 1_2_3_4_5_6_7_8.pin11, R3.Pin_1
  N19: Arduino_Mega.D29, 1_2_3_4_5_6_7_8.pin12, R4.Pin_1
  N20: Arduino_Mega.D31, 1_2_3_4_5_6_7_8.pin13, R6.Pin_1
  N21: Arduino_Mega.D33, 1_2_3_4_5_6_7_8.pin14, R7.Pin_1
  N22: Arduino_Mega.D35, 1_2_3_4_5_6_7_8.pin15, R8.Pin_1
  N23: Arduino_Mega.D37, 1_2_3_4_5_6_7_8.pin16, R9.Pin_1
  N24: Arduino_Mega.D38, DRV_2.ENABLE
  N25: Arduino_Mega.D39, DRV_8.DIRECTION
  N26: Arduino_Mega.D40, DRV_2.STEP
  N27: Arduino_Mega.D41, DRV_8.STEP
  N28: Arduino_Mega.D42, DRV_2.DIRECTION
  N29: Arduino_Mega.D43, DRV_8.ENABLE
  N30: Arduino_Mega.D44, DRV_4.ENABLE
  N31: Arduino_Mega.D45, DRV_6.ENABLE
  N32: Arduino_Mega.D46, DRV_4.STEP
  N33: Arduino_Mega.D47, DRV_6.STEP
  N34: Arduino_Mega.D48, DRV_4.DIRECTION
  N35: Arduino_Mega.D49, DRV_6.DIRECTION
  N36: Arduino_Mega.D50, DRV_5.ENABLE
  N37: Arduino_Mega.D51, DRV_7.DIRECTION
  N38: Arduino_Mega.D52, DRV_5.STEP
  N39: Arduino_Mega.D53, DRV_7.STEP
  N40: DRV_4.OUT_2B, 4.pin1
  N41: DRV_4.OUT_2A, 4.pin2
  N42: DRV_4.OUT_1A, 4.pin3
  N43: DRV_4.OUT_1B, 4.pin4
  N44: DRV_1.OUT_2B, 1.pin1
  N45: DRV_1.OUT_2A, 1.pin2
  N46: DRV_1.OUT_1A, 1.pin3
  N47: DRV_1.OUT_1B, 1.pin4
  N48: DRV_2.OUT_2B, 2.pin1
  N49: DRV_2.OUT_2A, 2.pin2
  N50: DRV_2.OUT_1A, 2.pin3
  N51: DRV_2.OUT_1B, 2.pin4
  N52: DRV_5.VOLTAGE_ST/_MT, DRV_6.VOLTAGE_ST/_MT, DRV_7.VOLTAGE_ST/_MT, DRV_8.VOLTAGE_ST/_MT, +12-_2.pin2, C1.+
  N53: DRV_5.GROUND_ST/_MT, DRV_6.GROUND_ST/_MT, DRV_7.GROUND_ST/_MT, DRV_8.GROUND_ST/_MT, +12-_2.pin1, C1.-
  N54: DRV_5.OUT_2B, 5.pin1
  N55: DRV_5.OUT_2A, 5.pin2
  N56: DRV_5.OUT_1A, 5.pin3
  N57: DRV_5.OUT_1B, 5.pin4
  N58: DRV_6.OUT_2B, 6.pin1
  N59: DRV_6.OUT_2A, 6.pin2
  N60: DRV_6.OUT_1A, 6.pin3
  N61: DRV_6.OUT_1B, 6.pin4
  N62: DRV_7.OUT_2B, 7.pin1
  N63: DRV_7.OUT_2A, 7.pin2
  N64: DRV_7.OUT_1A, 7.pin3
  N65: DRV_7.OUT_1B, 7.pin4
  N66: DRV_8.OUT_2B, 8.pin1
  N67: DRV_8.OUT_2A, 8.pin2
  N68: DRV_8.OUT_1A, 8.pin3
  N69: DRV_8.OUT_1B, 8.pin4
  N70: +12-_3.pin1, +FAN-.pin1, +FAN-_2.pin1
  N71: +12-_3.pin2, +FAN-.pin2, +FAN-_2.pin2

notes:
  HackBerry Lab || Event Horizon Stepper Driver 1.0
